// Logisim project MUX-8-to-1-using-two-4-to-1-MUX.circ as structural Verilog: 1 circuit, main circuit main
module main (
  input  I0,
  input  I1,
  input  I2,
  input  I3,
  input  E,
  input  [1:0] in_6,
  input  I4,
  input  I5,
  input  I6,
  input  I7,
  output OUTPUT
);

  wire multiplexer_1_out, multiplexer_2_out, not_1_out;

  Multiplexer #(.select(2)) multiplexer_1 (
    .in0(I0), .in1(I1), .in2(I2), .in3(I3), .out(multiplexer_1_out), .sel(in_6), .en(E));
  not not_1 (not_1_out, E);
  Multiplexer #(.select(2)) multiplexer_2 (
    .in0(I4), .in1(I5), .in2(I6), .in3(I7), .out(multiplexer_2_out), .sel(in_6), .en(not_1_out));
  Multiplexer multiplexer_3 (
    .in0(multiplexer_1_out), .in1(multiplexer_2_out), .out(OUTPUT), .sel(not_1_out), .en(1'b1));
endmodule
