// Logisim project circuit.circ as structural Verilog: 12 circuits, main circuit main
module main (
  input  in_1,
  output [5:0] No__of_successful_run,
  output [5:0] No__of_non_successful_run
);

  wire a_and_v_generator_1_v_s_carry, acceleration_1_successful_acceleration, and_1_out, and_2_out,
       and_3_out, between_1_if_1_then_yes, between_2_if_1_then_yes, clock_1_out,
       deceleration_1_successful_diceleration, not_1_out, not_2_out, or_1_out;
  wire [2:0] a_and_v_generator_1_a, a_and_v_generator_1_v;

  Clock clock_1 (.out(clock_1_out));
  A_and_V_Generator a_and_v_generator_1 (
    .Clock(clock_1_out), .Reset(in_1), .V(a_and_v_generator_1_v), .A(a_and_v_generator_1_a),
    .V_s_Carry(a_and_v_generator_1_v_s_carry));
  not not_1 (not_1_out, a_and_v_generator_1_v_s_carry);
  and and_1 (and_1_out, not_1_out, clock_1_out);
  Between between_1 (
    .Number(a_and_v_generator_1_a), .Lower_Bound(3'b001), .Upper_Bound(3'b011),
    .If_1_then_yes(between_1_if_1_then_yes));
  Between between_2 (
    .Number(a_and_v_generator_1_a), .Lower_Bound(3'b100), .Upper_Bound(3'b110),
    .If_1_then_yes(between_2_if_1_then_yes));
  and and_2 (and_2_out, between_1_if_1_then_yes, deceleration_1_successful_diceleration);
  Deceleration deceleration_1 (
    .Enable(between_1_if_1_then_yes), .V(a_and_v_generator_1_v), .A(a_and_v_generator_1_a),
    .Successful_Diceleration(deceleration_1_successful_diceleration));
  and and_3 (and_3_out, between_2_if_1_then_yes, acceleration_1_successful_acceleration);
  Acceleration acceleration_1 (
    .Enable(between_2_if_1_then_yes), .V(a_and_v_generator_1_v), .A(a_and_v_generator_1_a),
    .Successful_Acceleration(acceleration_1_successful_acceleration));
  LED Decelerates (.in(and_2_out));
  LED Accelerate (.in(and_3_out));
  or or_1 (or_1_out, and_3_out, and_2_out);
  LED Successful (.in(or_1_out));
  Counter #(.width(6), .max('h3f), .ongoal("stay")) counter_1 (
    .count(or_1_out), .Q(No__of_successful_run), .clk(and_1_out));  // open: load, D, carry, clr
  not not_2 (not_2_out, or_1_out);
  Counter #(.width(6), .max('h3f), .ongoal("stay")) counter_2 (
    .count(not_2_out), .Q(No__of_non_successful_run), .clk(and_1_out));  // open: load, D, carry, clr
endmodule

// 3 Bit OR Gate
module _3_Bit_OR (
  input  A,
  input  B,
  input  C,
  output Output
);

  wire or_1_out;

  or or_1 (or_1_out, A, B);
  or or_2 (Output, or_1_out, C);
endmodule

module Subtractor_1_Bit (
  input  A,
  input  B,
  input  Bin,
  output Difference,
  output Borrow
);

  wire and_1_out, and_2_out, and_3_out, and_4_out, and_5_out, and_6_out, and_7_out, and_8_out, and_9_out,
       and_10_out, and_11_out, not_1_out, not_2_out, not_3_out, not_4_out, not_5_out, not_6_out, not_7_out,
       not_8_out, or_1_out, or_2_out, or_3_out;

  not not_1 (not_1_out, A);
  not not_2 (not_2_out, B);
  not not_3 (not_3_out, A);
  not not_4 (not_4_out, B);
  not not_5 (not_5_out, A);
  not not_6 (not_6_out, A);
  and and_1 (and_1_out, not_1_out, not_2_out);
  and and_2 (and_2_out, not_3_out, B);
  not not_7 (not_7_out, Bin);
  and and_3 (and_3_out, A, not_4_out);
  not not_8 (not_8_out, Bin);
  and and_4 (and_4_out, A, B);
  and and_5 (and_5_out, not_5_out, Bin);
  and and_6 (and_6_out, not_6_out, B);
  and and_7 (and_7_out, and_1_out, Bin);
  and and_8 (and_8_out, and_2_out, not_7_out);
  and and_9 (and_9_out, and_3_out, not_8_out);
  and and_10 (and_10_out, and_4_out, Bin);
  or or_1 (or_1_out, and_5_out, and_6_out);
  and and_11 (and_11_out, B, Bin);
  or or_2 (or_2_out, and_7_out, and_8_out);
  or or_3 (or_3_out, and_9_out, and_10_out);
  or or_4 (Borrow, or_1_out, and_11_out);
  or or_5 (Difference, or_2_out, or_3_out);
endmodule

// Subtractor
module Subtractor_3_Bits (
  input  Enable,
  input  [2:0] A,
  input  [2:0] B,
  output [2:0] Difference,
  output Borrow
);

  wire and_1_out, and_2_out, and_3_out, and_4_out, and_5_out, and_6_out, subtractor_1_bit_1_borrow,
       subtractor_1_bit_2_borrow;

  and and_1 (and_1_out, Enable, A[0]);
  and and_2 (and_2_out, Enable, A[1]);
  and and_3 (and_3_out, Enable, A[2]);
  and and_4 (and_4_out, Enable, B[0]);
  and and_5 (and_5_out, Enable, B[1]);
  and and_6 (and_6_out, Enable, B[2]);
  Subtractor_1_Bit subtractor_1_bit_1 (
    .A(and_1_out), .B(and_4_out), .Bin(1'b0), .Difference(Difference[0]), .Borrow(subtractor_1_bit_1_borrow));
  Subtractor_1_Bit subtractor_1_bit_2 (
    .A(and_2_out), .B(and_5_out), .Bin(subtractor_1_bit_1_borrow), .Difference(Difference[1]),
    .Borrow(subtractor_1_bit_2_borrow));
  Subtractor_1_Bit subtractor_1_bit_3 (
    .A(and_3_out), .B(and_6_out), .Bin(subtractor_1_bit_2_borrow), .Difference(Difference[2]), .Borrow(Borrow));
endmodule

module Comparator_1_Bit (
  input  Enable,
  input  A,
  input  B,
  output AB,
  output AB2,
  output AB3
);

  wire and_1_out, and_2_out, and_3_out, and_4_out, and_7_out, and_8_out, not_1_out, not_2_out, not_3_out,
       not_4_out;

  not not_1 (not_1_out, A);
  not not_2 (not_2_out, A);
  and and_1 (and_1_out, Enable, A);
  not not_3 (not_3_out, B);
  and and_2 (and_2_out, Enable, not_1_out);
  and and_3 (and_3_out, Enable, not_2_out);
  not not_4 (not_4_out, B);
  and and_4 (and_4_out, Enable, A);
  and and_5 (AB3, and_1_out, not_3_out);
  and and_6 (AB, and_2_out, B);
  and and_7 (and_7_out, and_3_out, not_4_out);
  and and_8 (and_8_out, and_4_out, B);
  or or_1 (AB2, and_7_out, and_8_out);
endmodule

module Comparator_3_Bits (
  input  Enable,
  input  [2:0] A,
  input  [2:0] B,
  output A___B,
  output A___B_2,
  output A___B_3
);

  wire comparator_1_bit_1_ab, comparator_1_bit_1_ab2, comparator_1_bit_1_ab3, comparator_1_bit_2_ab,
       comparator_1_bit_2_ab2, comparator_1_bit_2_ab3, comparator_1_bit_3_ab, comparator_1_bit_3_ab3;

  Comparator_1_Bit comparator_1_bit_1 (
    .Enable(Enable), .A(A[2]), .B(B[2]), .AB(comparator_1_bit_1_ab), .AB2(comparator_1_bit_1_ab2),
    .AB3(comparator_1_bit_1_ab3));
  Comparator_1_Bit comparator_1_bit_2 (
    .Enable(comparator_1_bit_1_ab2), .A(A[1]), .B(B[1]), .AB(comparator_1_bit_2_ab),
    .AB2(comparator_1_bit_2_ab2), .AB3(comparator_1_bit_2_ab3));
  Comparator_1_Bit comparator_1_bit_3 (
    .Enable(comparator_1_bit_2_ab2), .A(A[0]), .B(B[0]), .AB(comparator_1_bit_3_ab), .AB2(A___B_2),
    .AB3(comparator_1_bit_3_ab3));
  _3_Bit_OR u_3_bit_or_1 (
    .A(comparator_1_bit_1_ab3), .B(comparator_1_bit_2_ab3), .C(comparator_1_bit_3_ab3), .Output(A___B_3));
  _3_Bit_OR u_3_bit_or_2 (
    .A(comparator_1_bit_1_ab), .B(comparator_1_bit_2_ab), .C(comparator_1_bit_3_ab), .Output(A___B));
endmodule

module Between (
  input  [2:0] Number,
  input  [2:0] Lower_Bound,
  input  [2:0] Upper_Bound,
  output If_1_then_yes
);

  wire comparator_3_bits_1_a___b, comparator_3_bits_2_a___b, comparator_3_bits_2_a___b_2,
       comparator_3_bits_3_a___b_2, comparator_3_bits_3_a___b_3, or_1_out, or_2_out;

  Comparator_3_Bits comparator_3_bits_1 (
    .A(Lower_Bound), .B(Upper_Bound), .Enable(1'b1), .A___B(comparator_3_bits_1_a___b));  // open: A___B_2, A___B_3
  Comparator_3_Bits comparator_3_bits_2 (
    .A(Number), .B(Upper_Bound), .Enable(comparator_3_bits_1_a___b), .A___B(comparator_3_bits_2_a___b),
    .A___B_2(comparator_3_bits_2_a___b_2));  // open: A___B_3
  Comparator_3_Bits comparator_3_bits_3 (
    .A(Number), .B(Lower_Bound), .Enable(comparator_3_bits_1_a___b), .A___B_2(comparator_3_bits_3_a___b_2),
    .A___B_3(comparator_3_bits_3_a___b_3));  // open: A___B
  or or_1 (or_1_out, comparator_3_bits_3_a___b_2, comparator_3_bits_3_a___b_3);
  and and_1 (If_1_then_yes, or_1_out, or_2_out);
  or or_2 (or_2_out, comparator_3_bits_2_a___b, comparator_3_bits_2_a___b_2);
endmodule

module Adder_1_Bit (
  input  A,
  input  B,
  input  Cin,
  output Sum,
  output Carry
);

  wire and_1_out, and_2_out, and_3_out, and_4_out, and_5_out, and_6_out, and_7_out, and_8_out, and_9_out,
       and_10_out, and_11_out, not_1_out, not_2_out, not_3_out, not_4_out, not_5_out, not_6_out, or_1_out,
       or_3_out, or_4_out;

  not not_1 (not_1_out, A);
  not not_2 (not_2_out, B);
  not not_3 (not_3_out, A);
  not not_4 (not_4_out, B);
  and and_1 (and_1_out, B, Cin);
  and and_2 (and_2_out, A, Cin);
  and and_3 (and_3_out, not_1_out, not_2_out);
  and and_4 (and_4_out, not_3_out, B);
  not not_5 (not_5_out, Cin);
  and and_5 (and_5_out, A, not_4_out);
  not not_6 (not_6_out, Cin);
  and and_6 (and_6_out, A, B);
  or or_1 (or_1_out, and_1_out, and_2_out);
  and and_7 (and_7_out, A, B);
  and and_8 (and_8_out, and_3_out, Cin);
  and and_9 (and_9_out, and_4_out, not_5_out);
  and and_10 (and_10_out, and_5_out, not_6_out);
  and and_11 (and_11_out, and_6_out, Cin);
  or or_2 (Carry, or_1_out, and_7_out);
  or or_3 (or_3_out, and_8_out, and_9_out);
  or or_4 (or_4_out, and_10_out, and_11_out);
  or or_5 (Sum, or_3_out, or_4_out);
endmodule

// Adder
module Adder_3_Bits (
  input  Enable,
  input  [2:0] A,
  input  [2:0] B,
  output [2:0] Sum,
  output Carry
);

  wire adder_1_bit_1_carry, adder_1_bit_2_carry, and_1_out, and_2_out, and_3_out, and_4_out, and_5_out,
       and_6_out;

  and and_1 (and_1_out, Enable, A[0]);
  and and_2 (and_2_out, Enable, A[1]);
  and and_3 (and_3_out, Enable, A[2]);
  and and_4 (and_4_out, Enable, B[0]);
  and and_5 (and_5_out, Enable, B[1]);
  and and_6 (and_6_out, Enable, B[2]);
  Adder_1_Bit adder_1_bit_1 (.A(and_1_out), .B(and_4_out), .Cin(1'b0), .Sum(Sum[0]), .Carry(adder_1_bit_1_carry));
  Adder_1_Bit adder_1_bit_2 (
    .A(and_2_out), .B(and_5_out), .Cin(adder_1_bit_1_carry), .Sum(Sum[1]), .Carry(adder_1_bit_2_carry));
  Adder_1_Bit adder_1_bit_3 (.A(and_3_out), .B(and_6_out), .Cin(adder_1_bit_2_carry), .Sum(Sum[2]), .Carry(Carry));
endmodule

module A_and_V_Generator (
  input  Clock,
  input  Reset,
  output [2:0] V,
  output [2:0] A,
  output V_s_Carry
);

  wire A_carry, not_1_out, or_1_out;

  Counter #(.width(3), .max('h7), .ongoal("stay")) u_V (
    .Q(V), .carry(V_s_Carry), .clk(A_carry), .clr(Reset));  // open: load, D, count
  Counter #(.width(3), .max('h7)) u_A (
    .count(1'b1), .Q(A), .carry(A_carry), .clk(not_1_out), .clr(Reset));  // open: load, D
  not not_1 (not_1_out, or_1_out);
  or or_1 (or_1_out, Clock, V_s_Carry);
endmodule

module Acceleration (
  input  Enable,
  input  [2:0] V,
  input  [2:0] A,
  output Successful_Acceleration
);

  wire adder_3_bits_1_carry;
  wire [2:0] subtractor_3_bits_1_difference;

  Subtractor_3_Bits subtractor_3_bits_1 (
    .Enable(Enable), .A(A), .B(3'b011), .Difference(subtractor_3_bits_1_difference));  // open: Borrow
  Adder_3_Bits adder_3_bits_1 (
    .Enable(Enable), .A(V), .B(subtractor_3_bits_1_difference), .Carry(adder_3_bits_1_carry));  // open: Sum
  not not_1 (Successful_Acceleration, adder_3_bits_1_carry);
endmodule

module Deceleration (
  input  Enable,
  input  [2:0] V,
  input  [2:0] A,
  output Successful_Diceleration
);

  wire subtractor_3_bits_1_borrow;

  Subtractor_3_Bits subtractor_3_bits_1 (
    .Enable(Enable), .A(V), .B(A), .Borrow(subtractor_3_bits_1_borrow));  // open: Difference
  not not_1 (Successful_Diceleration, subtractor_3_bits_1_borrow);
endmodule
