// Logisim project circuit.circ as structural Verilog: 3 circuits, main circuit main
module main (
  input  [2:0] V,
  input  [2:0] A,
  input  Reset,
  output [5:0] No_of_successful_run,
  output [5:0] No_of_non_successful_run
);

  wire Clock_Button_out;

  Button Clock_Button (.out(Clock_Button_out));
  PART_B part_b_1 (
    .V(V), .A(A), .Clock(Clock_Button_out), .Reset__When_1__counter_starts_from_0(Reset),
    .No__of_successful_run(No_of_successful_run), .No__of_non_successful_run(No_of_non_successful_run));
endmodule

// Part A
module PART_A (
  input  [2:0] V,
  input  [2:0] A,
  output Successful
);

  wire and_1_out, and_2_out, and_3_out, and_4_out, and_5_out, and_6_out, and_7_out, and_8_out, and_9_out,
       and_10_out, and_11_out, and_12_out, and_13_out, and_14_out, and_15_out, and_16_out, and_17_out,
       and_18_out, and_19_out, and_20_out, and_21_out, not_1_out, not_2_out, not_3_out, not_4_out, not_5_out,
       not_6_out, not_7_out, not_8_out, not_9_out, not_10_out, not_11_out, not_12_out, not_13_out,
       not_14_out, not_15_out, not_16_out, or_1_out, or_2_out, or_3_out, or_4_out, or_5_out, or_6_out,
       or_7_out, or_8_out, or_9_out, or_10_out;

  not not_1 (not_1_out, V[2]);
  not not_2 (not_2_out, A[2]);
  not not_3 (not_3_out, V[2]);
  not not_4 (not_4_out, V[1]);
  not not_5 (not_5_out, A[1]);
  not not_6 (not_6_out, A[0]);
  and and_1 (and_1_out, not_1_out, A[2]);
  not not_7 (not_7_out, A[0]);
  not not_8 (not_8_out, V[1]);
  not not_9 (not_9_out, A[1]);
  and and_2 (and_2_out, V[0], A[2]);
  not not_10 (not_10_out, A[2]);
  and and_3 (and_3_out, V[1], not_2_out);
  not not_11 (not_11_out, A[0]);
  and and_4 (and_4_out, not_3_out, V[1]);
  and and_5 (and_5_out, V[2], not_4_out);
  not not_12 (not_12_out, V[0]);
  not not_13 (not_13_out, A[2]);
  and and_6 (and_6_out, not_5_out, not_6_out);
  and and_7 (and_7_out, and_1_out, not_7_out);
  and and_8 (and_8_out, not_8_out, A[2]);
  not not_14 (not_14_out, A[1]);
  and and_9 (and_9_out, V[0], not_9_out);
  and and_10 (and_10_out, and_2_out, A[0]);
  and and_11 (and_11_out, V[1], not_10_out);
  not not_15 (not_15_out, A[1]);
  and and_12 (and_12_out, and_3_out, not_11_out);
  and and_13 (and_13_out, and_4_out, A[2]);
  and and_14 (and_14_out, V[1], V[0]);
  not not_16 (not_16_out, A[2]);
  and and_15 (and_15_out, and_5_out, not_12_out);
  and and_16 (and_16_out, V[2], not_13_out);
  and and_17 (and_17_out, V[2], A[1]);
  or or_1 (or_1_out, and_6_out, and_7_out);
  or or_2 (or_2_out, or_1_out, and_18_out);
  and and_18 (and_18_out, and_8_out, not_14_out);
  or or_3 (or_3_out, and_9_out, and_10_out);
  or or_4 (or_4_out, or_3_out, and_19_out);
  and and_19 (and_19_out, and_11_out, not_15_out);
  or or_5 (or_5_out, and_12_out, and_13_out);
  or or_6 (or_6_out, or_5_out, and_20_out);
  and and_20 (and_20_out, and_14_out, not_16_out);
  or or_7 (or_7_out, and_15_out, and_16_out);
  or or_8 (or_8_out, or_7_out, and_21_out);
  and and_21 (and_21_out, and_17_out, A[0]);
  or or_9 (or_9_out, or_2_out, or_4_out);
  or or_10 (or_10_out, or_6_out, or_8_out);
  or or_11 (Successful, or_9_out, or_10_out);
endmodule

// Part B
module PART_B (
  input  [2:0] V,
  input  [2:0] A,
  input  Clock,
  input  Reset__When_1__counter_starts_from_0,
  output [5:0] No__of_successful_run,
  output [5:0] No__of_non_successful_run
);

  wire not_1_out, part_a_1_successful;

  PART_A part_a_1 (.V(V), .A(A), .Successful(part_a_1_successful));
  Counter #(.width(6), .max('h3f), .ongoal("stay")) counter_1 (
    .count(part_a_1_successful), .Q(No__of_successful_run), .clk(Clock),
    .clr(Reset__When_1__counter_starts_from_0));  // open: load, D, carry
  not not_1 (not_1_out, part_a_1_successful);
  Counter #(.width(6), .max('h3f), .ongoal("stay")) counter_2 (
    .count(not_1_out), .clk(Clock), .clr(Reset__When_1__counter_starts_from_0));  // open: load, D, Q, carry
endmodule
