// Logisim project circuit.circ as structural Verilog: 3 circuits, main circuit main
module main (
  output SUCCESSFUL,
  output [5:0] SUCCESSFULL_RUNS,
  output [5:0] UNSUCCESSFUL_RUNS
);

  wire and_1_out, CLOCK_out, key_and_locker_generator_1_k0, key_and_locker_generator_1_k1,
       key_and_locker_generator_1_k2, key_and_locker_generator_1_k_s_carry, key_and_locker_generator_1_l0,
       key_and_locker_generator_1_l1, key_and_locker_generator_1_l2, not_1_out, not_2_out;

  KEY_AND_LOCKER_GENERATOR key_and_locker_generator_1 (
    .Clock(CLOCK_out), .K0(key_and_locker_generator_1_k0), .K1(key_and_locker_generator_1_k1),
    .K2(key_and_locker_generator_1_k2), .L0(key_and_locker_generator_1_l0),
    .L1(key_and_locker_generator_1_l1), .L2(key_and_locker_generator_1_l2),
    .K_s_Carry(key_and_locker_generator_1_k_s_carry));  // open: Reset
  Clock CLOCK (.out(CLOCK_out));
  not not_1 (not_1_out, key_and_locker_generator_1_k_s_carry);
  and and_1 (and_1_out, not_1_out, CLOCK_out);
  PART_A part_a_1 (
    .K0(key_and_locker_generator_1_k0), .K1(key_and_locker_generator_1_k1),
    .K2(key_and_locker_generator_1_k2), .L0(key_and_locker_generator_1_l0),
    .L1(key_and_locker_generator_1_l1), .L2(key_and_locker_generator_1_l2), .SUCCESSFUL(SUCCESSFUL));
  Counter #(.width(6), .max('h3f), .ongoal("stay")) counter_1 (
    .count(SUCCESSFUL), .Q(SUCCESSFULL_RUNS), .clk(and_1_out));  // open: load, D, carry, clr
  not not_2 (not_2_out, SUCCESSFUL);
  Counter #(.width(6), .max('h3f), .ongoal("stay")) counter_2 (
    .count(not_2_out), .Q(UNSUCCESSFUL_RUNS), .clk(and_1_out));  // open: load, D, carry, clr
  LED SIMULATION_STOPPED (.in(key_and_locker_generator_1_k_s_carry));
endmodule

// COMBINATION CHECKER
module PART_A (
  input  K0,
  input  K1,
  input  K2,
  input  L0,
  input  L1,
  input  L2,
  output SUCCESSFUL
);

  wire decoder_1_out0, decoder_1_out1, decoder_1_out2, decoder_1_out3, decoder_1_out4, decoder_1_out5,
       decoder_1_out6, decoder_1_out7, decoder_2_out0, decoder_2_out1, decoder_2_out2, decoder_2_out3,
       decoder_2_out4, decoder_2_out5, decoder_2_out6, decoder_2_out7, K0_L0_out, K0_L1_out, K0_L2_out,
       K0_L3_out, K0_L4_out, K0_L5_out, K0_L6_out, K0_L7_out, K1_L1_out, K2_L2_out, K3_L3_out, K4_L4_out,
       K5_L5_out, K6_L1_out, K6_L2_out, K6_L3_out, K6_L6_out, K7_L4_out, K7_L5_out, K7_L7_out, or_1_out,
       or_2_out, or_3_out, or_4_out, or_5_out, or_6_out, or_7_out, or_8_out, or_9_out, or_10_out, or_11_out,
       or_12_out, or_13_out, or_14_out, or_15_out, or_16_out, or_17_out, or_18_out;

  Decoder #(.select(3)) decoder_1 (
    .out0(decoder_1_out0), .out1(decoder_1_out1), .out2(decoder_1_out2), .out3(decoder_1_out3),
    .out4(decoder_1_out4), .out5(decoder_1_out5), .out6(decoder_1_out6), .out7(decoder_1_out7),
    .sel({K2, K1, K0}), .en(1'b1));
  Decoder #(.select(3)) decoder_2 (
    .out0(decoder_2_out0), .out1(decoder_2_out1), .out2(decoder_2_out2), .out3(decoder_2_out3),
    .out4(decoder_2_out4), .out5(decoder_2_out5), .out6(decoder_2_out6), .out7(decoder_2_out7),
    .sel({L2, L1, L0}), .en(1'b1));
  and K0_L0 (K0_L0_out, decoder_1_out0, decoder_2_out0);
  or or_1 (or_1_out, K0_L0_out, K0_L1_out);
  and K0_L1 (K0_L1_out, decoder_1_out0, decoder_2_out1);
  and K0_L2 (K0_L2_out, decoder_1_out0, decoder_2_out2);
  or or_2 (or_2_out, K0_L2_out, K0_L3_out);
  and K0_L3 (K0_L3_out, decoder_1_out0, decoder_2_out3);
  and K0_L4 (K0_L4_out, decoder_1_out0, decoder_2_out4);
  or or_3 (or_3_out, K0_L4_out, K0_L5_out);
  and K0_L5 (K0_L5_out, decoder_1_out0, decoder_2_out5);
  and K0_L6 (K0_L6_out, decoder_1_out0, decoder_2_out6);
  or or_4 (or_4_out, K0_L6_out, K0_L7_out);
  and K0_L7 (K0_L7_out, decoder_1_out0, decoder_2_out7);
  and K1_L1 (K1_L1_out, decoder_1_out1, decoder_2_out1);
  or or_5 (or_5_out, K1_L1_out, K2_L2_out);
  and K2_L2 (K2_L2_out, decoder_1_out2, decoder_2_out2);
  and K3_L3 (K3_L3_out, decoder_1_out3, decoder_2_out3);
  or or_6 (or_6_out, K3_L3_out, K4_L4_out);
  and K4_L4 (K4_L4_out, decoder_1_out4, decoder_2_out4);
  and K5_L5 (K5_L5_out, decoder_1_out5, decoder_2_out5);
  or or_7 (or_7_out, K5_L5_out, K6_L1_out);
  and K6_L1 (K6_L1_out, decoder_1_out6, decoder_2_out1);
  and K6_L2 (K6_L2_out, decoder_1_out6, decoder_2_out2);
  or or_8 (or_8_out, K6_L2_out, K6_L3_out);
  and K6_L3 (K6_L3_out, decoder_1_out6, decoder_2_out3);
  and K6_L6 (K6_L6_out, decoder_1_out6, decoder_2_out6);
  or or_9 (or_9_out, K6_L6_out, K7_L4_out);
  and K7_L4 (K7_L4_out, decoder_1_out7, decoder_2_out4);
  and K7_L5 (K7_L5_out, decoder_1_out7, decoder_2_out5);
  or or_10 (or_10_out, K7_L5_out, K7_L7_out);
  and K7_L7 (K7_L7_out, decoder_1_out7, decoder_2_out7);
  or or_11 (or_11_out, or_1_out, or_2_out);
  or or_12 (or_12_out, or_3_out, or_4_out);
  or or_13 (or_13_out, or_5_out, or_6_out);
  or or_14 (or_14_out, or_13_out, or_15_out);
  or or_15 (or_15_out, or_7_out, or_8_out);
  or or_16 (or_16_out, or_9_out, or_10_out);
  or or_17 (or_17_out, or_11_out, or_12_out);
  or or_18 (or_18_out, or_14_out, or_16_out);
  or or_19 (SUCCESSFUL, or_17_out, or_18_out);
endmodule

// COMBO GENERATOR
module KEY_AND_LOCKER_GENERATOR (
  input  Clock,
  input  Reset,
  output K0,
  output K1,
  output K2,
  output L0,
  output L1,
  output L2,
  output K_s_Carry
);

  wire L_carry, not_1_out, or_1_out;

  Counter #(.width(3), .max('h7), .ongoal("stay")) K (
    .Q({K2, K1, K0}), .carry(K_s_Carry), .clk(L_carry), .clr(Reset));  // open: load, D, count
  Counter #(.width(3), .max('h7)) L (
    .count(1'b1), .Q({L2, L1, L0}), .carry(L_carry), .clk(not_1_out), .clr(Reset));  // open: load, D
  not not_1 (not_1_out, or_1_out);
  or or_1 (or_1_out, Clock, K_s_Carry);
endmodule
