// Logisim project circuit.circ as structural Verilog: 1 circuit, main circuit main
module main (
  input  A,
  input  B,
  input  C,
  output Parity_checked,
  output Parity
);

  wire xor_1_out, xor_3_out, xor_4_out;

  xor xor_1 (xor_1_out, A, B);
  xor xor_2 (Parity, xor_1_out, C);
  xor xor_3 (xor_3_out, A, B);
  xor xor_4 (xor_4_out, C, Parity);
  xor xor_5 (Parity_checked, xor_3_out, xor_4_out);

  // Notes on the sheet:
  //   Even parity bit generator
  //   Even parity bit checker
endmodule
