// Logisim project circuit.circ as structural Verilog: 3 circuits, main circuit main
module main (
  input  [4:0] Input,
  input  [4:0] Input_2,
  input  [5:0] Some_Malicious_bit,
  output Is_Data_Changed,
  output Is_Data_Changed_2
);

  wire [5:0] generator_or_sender_1_output, generator_or_sender_2_output, or_1_out;

  Generator_Or_Sender generator_or_sender_1 (._5_Bits_Input(Input), .Output(generator_or_sender_1_output));
  Generator_Or_Sender generator_or_sender_2 (._5_Bits_Input(Input_2), .Output(generator_or_sender_2_output));
  Checker_Or_Receiver checker_or_receiver_1 (
    .Received_6_Bits_Message(generator_or_sender_1_output), .Is_Data_Changed(Is_Data_Changed));
  assign or_1_out = generator_or_sender_2_output | Some_Malicious_bit;  // OR_Gate or_1, 6 bits wide
  Checker_Or_Receiver checker_or_receiver_2 (.Received_6_Bits_Message(or_1_out), .Is_Data_Changed(Is_Data_Changed_2));

  // Notes on the sheet:
  //   Case 2: If we change the data
  //   Case 1: If we don't change the data
endmodule

module Generator_Or_Sender (
  input  [4:0] _5_Bits_Input,
  output [5:0] Output
);

  wire nand_1_out, nand_2_out, nand_3_out, nand_4_out, nand_5_out, nand_6_out, nand_7_out, nand_8_out,
       nand_9_out, nand_10_out, nand_11_out, nand_12_out, nand_13_out, nand_14_out, nand_15_out, nand_16_out,
       nand_17_out, nand_18_out, nand_19_out, nand_20_out, nand_21_out, nand_22_out, nand_23_out,
       nand_24_out, nand_25_out, nand_26_out, nand_27_out, nand_28_out, nand_29_out, nand_30_out,
       nand_31_out, nand_32_out, nand_33_out, nand_34_out, nand_35_out, nand_36_out, nand_37_out,
       nand_38_out, nand_39_out, nand_40_out, nand_41_out, nand_42_out, nand_43_out, nand_44_out,
       nand_45_out, nand_46_out, nand_47_out, nand_48_out, nand_49_out, nand_50_out, nand_51_out,
       nand_52_out, nand_53_out, nand_54_out, nand_55_out, nand_56_out;

  nand nand_1 (nand_1_out, _5_Bits_Input[0], _5_Bits_Input[0]);
  nand nand_2 (nand_2_out, _5_Bits_Input[1], _5_Bits_Input[1]);
  nand nand_3 (nand_3_out, _5_Bits_Input[2], _5_Bits_Input[2]);
  nand nand_4 (nand_4_out, _5_Bits_Input[3], _5_Bits_Input[3]);
  nand nand_5 (nand_5_out, _5_Bits_Input[0], _5_Bits_Input[0]);
  nand nand_6 (nand_6_out, _5_Bits_Input[1], _5_Bits_Input[1]);
  nand nand_7 (nand_7_out, _5_Bits_Input[2], _5_Bits_Input[2]);
  nand nand_8 (nand_8_out, _5_Bits_Input[4], _5_Bits_Input[4]);
  nand nand_9 (nand_9_out, _5_Bits_Input[0], _5_Bits_Input[0]);
  nand nand_10 (nand_10_out, _5_Bits_Input[1], _5_Bits_Input[1]);
  nand nand_11 (nand_11_out, _5_Bits_Input[3], _5_Bits_Input[3]);
  nand nand_12 (nand_12_out, _5_Bits_Input[4], _5_Bits_Input[4]);
  nand nand_13 (nand_13_out, _5_Bits_Input[0], _5_Bits_Input[0]);
  nand nand_14 (nand_14_out, _5_Bits_Input[1], _5_Bits_Input[1]);
  nand nand_15 (nand_15_out, _5_Bits_Input[0], _5_Bits_Input[0]);
  nand nand_16 (nand_16_out, _5_Bits_Input[2], _5_Bits_Input[2]);
  nand nand_17 (nand_17_out, _5_Bits_Input[3], _5_Bits_Input[3]);
  nand nand_18 (nand_18_out, _5_Bits_Input[4], _5_Bits_Input[4]);
  nand nand_19 (nand_19_out, _5_Bits_Input[0], _5_Bits_Input[0]);
  nand nand_20 (nand_20_out, _5_Bits_Input[2], _5_Bits_Input[2]);
  nand nand_21 (nand_21_out, _5_Bits_Input[0], _5_Bits_Input[0]);
  nand nand_22 (nand_22_out, _5_Bits_Input[3], _5_Bits_Input[3]);
  nand nand_23 (nand_23_out, _5_Bits_Input[0], _5_Bits_Input[0]);
  nand nand_24 (nand_24_out, _5_Bits_Input[4], _5_Bits_Input[4]);
  nand nand_25 (nand_25_out, _5_Bits_Input[1], _5_Bits_Input[1]);
  nand nand_26 (nand_26_out, _5_Bits_Input[2], _5_Bits_Input[2]);
  nand nand_27 (nand_27_out, _5_Bits_Input[3], _5_Bits_Input[3]);
  nand nand_28 (nand_28_out, _5_Bits_Input[4], _5_Bits_Input[4]);
  nand nand_29 (nand_29_out, _5_Bits_Input[1], _5_Bits_Input[1]);
  nand nand_30 (nand_30_out, _5_Bits_Input[2], _5_Bits_Input[2]);
  nand nand_31 (nand_31_out, _5_Bits_Input[1], _5_Bits_Input[1]);
  nand nand_32 (nand_32_out, _5_Bits_Input[3], _5_Bits_Input[3]);
  nand nand_33 (nand_33_out, _5_Bits_Input[1], _5_Bits_Input[1]);
  nand nand_34 (nand_34_out, _5_Bits_Input[4], _5_Bits_Input[4]);
  nand nand_35 (nand_35_out, _5_Bits_Input[2], _5_Bits_Input[2]);
  nand nand_36 (nand_36_out, _5_Bits_Input[3], _5_Bits_Input[3]);
  nand nand_37 (nand_37_out, _5_Bits_Input[2], _5_Bits_Input[2]);
  nand nand_38 (nand_38_out, _5_Bits_Input[4], _5_Bits_Input[4]);
  nand nand_39 (nand_39_out, _5_Bits_Input[3], _5_Bits_Input[3]);
  nand nand_40 (nand_40_out, _5_Bits_Input[4], _5_Bits_Input[4]);
  nand nand_41 (nand_41_out, nand_1_out, nand_2_out, nand_3_out, nand_4_out, _5_Bits_Input[4]);
  nand nand_42 (nand_42_out, nand_5_out, nand_6_out, nand_7_out, _5_Bits_Input[3], nand_8_out);
  nand nand_43 (nand_43_out, nand_9_out, nand_10_out, _5_Bits_Input[2], nand_11_out, nand_12_out);
  nand nand_44 (nand_44_out, nand_13_out, nand_14_out, _5_Bits_Input[2], _5_Bits_Input[3], _5_Bits_Input[4]);
  nand nand_45 (nand_45_out, nand_15_out, _5_Bits_Input[1], nand_16_out, nand_17_out, nand_18_out);
  nand nand_46 (nand_46_out, nand_19_out, _5_Bits_Input[1], nand_20_out, _5_Bits_Input[3], _5_Bits_Input[4]);
  nand nand_47 (nand_47_out, nand_21_out, _5_Bits_Input[1], _5_Bits_Input[2], nand_22_out, _5_Bits_Input[4]);
  nand nand_48 (nand_48_out, nand_23_out, _5_Bits_Input[1], _5_Bits_Input[2], _5_Bits_Input[3], nand_24_out);
  nand nand_49 (nand_49_out, _5_Bits_Input[0], nand_25_out, nand_26_out, nand_27_out, nand_28_out);
  nand nand_50 (nand_50_out, _5_Bits_Input[0], nand_29_out, nand_30_out, _5_Bits_Input[3], _5_Bits_Input[4]);
  nand nand_51 (nand_51_out, _5_Bits_Input[0], nand_31_out, _5_Bits_Input[2], nand_32_out, _5_Bits_Input[4]);
  nand nand_52 (nand_52_out, _5_Bits_Input[0], nand_33_out, _5_Bits_Input[2], _5_Bits_Input[3], nand_34_out);
  nand nand_53 (nand_53_out, _5_Bits_Input[0], _5_Bits_Input[1], nand_35_out, nand_36_out, _5_Bits_Input[4]);
  nand nand_54 (nand_54_out, _5_Bits_Input[0], _5_Bits_Input[1], nand_37_out, _5_Bits_Input[3], nand_38_out);
  nand nand_55 (nand_55_out, _5_Bits_Input[0], _5_Bits_Input[1], _5_Bits_Input[2], nand_39_out, nand_40_out);
  nand nand_56 (nand_56_out, _5_Bits_Input[0], _5_Bits_Input[1], _5_Bits_Input[2], _5_Bits_Input[3], _5_Bits_Input[4]);
  nand nand_57 (Output[5], nand_41_out, nand_42_out, nand_43_out, nand_44_out, nand_45_out, nand_46_out, nand_47_out, nand_48_out, nand_49_out, nand_50_out, nand_51_out, nand_52_out, nand_53_out, nand_54_out, nand_55_out, nand_56_out);

  assign Output[4:0] = _5_Bits_Input;
endmodule

module Checker_Or_Receiver (
  input  [5:0] Received_6_Bits_Message,
  output Is_Data_Changed
);

  wire and_1_out, and_2_out, and_3_out, and_4_out, and_5_out, and_6_out, and_7_out, and_8_out, and_9_out,
       and_10_out, and_11_out, and_12_out, and_13_out, and_14_out, and_15_out, and_16_out, and_17_out,
       and_18_out, and_19_out, and_20_out, and_21_out, and_22_out, and_23_out, and_24_out, and_25_out,
       and_26_out, and_27_out, and_28_out, and_29_out, and_30_out, and_31_out, and_32_out, not_1_out,
       not_2_out, not_3_out, not_4_out, not_5_out, not_6_out, not_7_out, not_8_out, not_9_out, not_10_out,
       not_11_out, not_12_out, not_13_out, not_14_out, not_15_out, not_16_out, not_17_out, not_18_out,
       not_19_out, not_20_out, not_21_out, not_22_out, not_23_out, not_24_out, not_25_out, not_26_out,
       not_27_out, not_28_out, not_29_out, not_30_out, not_31_out, not_32_out, not_33_out, not_34_out,
       not_35_out, not_36_out, not_37_out, not_38_out, not_39_out, not_40_out, not_41_out, not_42_out,
       not_43_out, not_44_out, not_45_out, not_46_out, not_47_out, not_48_out, not_49_out, not_50_out,
       not_51_out, not_52_out, not_53_out, not_54_out, not_55_out, not_56_out, not_57_out, not_58_out,
       not_59_out, not_60_out, not_61_out, not_62_out, not_63_out, not_64_out, not_65_out, not_66_out,
       not_67_out, not_68_out, not_69_out, not_70_out, not_71_out, not_72_out, not_73_out, not_74_out,
       not_75_out, not_76_out, not_77_out, not_78_out, not_79_out, not_80_out, not_81_out, not_82_out,
       not_83_out, not_84_out, not_85_out, not_86_out, not_87_out, not_88_out, not_89_out, not_90_out,
       not_91_out, not_92_out, not_93_out, not_94_out, not_95_out, not_96_out;

  not not_1 (not_1_out, Received_6_Bits_Message[0]);
  not not_2 (not_2_out, Received_6_Bits_Message[1]);
  not not_3 (not_3_out, Received_6_Bits_Message[2]);
  not not_4 (not_4_out, Received_6_Bits_Message[3]);
  not not_5 (not_5_out, Received_6_Bits_Message[4]);
  not not_6 (not_6_out, Received_6_Bits_Message[0]);
  not not_7 (not_7_out, Received_6_Bits_Message[1]);
  not not_8 (not_8_out, Received_6_Bits_Message[2]);
  not not_9 (not_9_out, Received_6_Bits_Message[3]);
  not not_10 (not_10_out, Received_6_Bits_Message[5]);
  not not_11 (not_11_out, Received_6_Bits_Message[0]);
  not not_12 (not_12_out, Received_6_Bits_Message[1]);
  not not_13 (not_13_out, Received_6_Bits_Message[2]);
  not not_14 (not_14_out, Received_6_Bits_Message[4]);
  not not_15 (not_15_out, Received_6_Bits_Message[5]);
  not not_16 (not_16_out, Received_6_Bits_Message[0]);
  not not_17 (not_17_out, Received_6_Bits_Message[1]);
  not not_18 (not_18_out, Received_6_Bits_Message[2]);
  not not_19 (not_19_out, Received_6_Bits_Message[0]);
  not not_20 (not_20_out, Received_6_Bits_Message[1]);
  not not_21 (not_21_out, Received_6_Bits_Message[3]);
  not not_22 (not_22_out, Received_6_Bits_Message[4]);
  not not_23 (not_23_out, Received_6_Bits_Message[5]);
  not not_24 (not_24_out, Received_6_Bits_Message[0]);
  not not_25 (not_25_out, Received_6_Bits_Message[1]);
  not not_26 (not_26_out, Received_6_Bits_Message[3]);
  not not_27 (not_27_out, Received_6_Bits_Message[0]);
  not not_28 (not_28_out, Received_6_Bits_Message[1]);
  not not_29 (not_29_out, Received_6_Bits_Message[4]);
  not not_30 (not_30_out, Received_6_Bits_Message[0]);
  not not_31 (not_31_out, Received_6_Bits_Message[1]);
  not not_32 (not_32_out, Received_6_Bits_Message[5]);
  not not_33 (not_33_out, Received_6_Bits_Message[0]);
  not not_34 (not_34_out, Received_6_Bits_Message[2]);
  not not_35 (not_35_out, Received_6_Bits_Message[3]);
  not not_36 (not_36_out, Received_6_Bits_Message[4]);
  not not_37 (not_37_out, Received_6_Bits_Message[5]);
  not not_38 (not_38_out, Received_6_Bits_Message[0]);
  not not_39 (not_39_out, Received_6_Bits_Message[2]);
  not not_40 (not_40_out, Received_6_Bits_Message[3]);
  not not_41 (not_41_out, Received_6_Bits_Message[0]);
  not not_42 (not_42_out, Received_6_Bits_Message[2]);
  not not_43 (not_43_out, Received_6_Bits_Message[4]);
  not not_44 (not_44_out, Received_6_Bits_Message[0]);
  not not_45 (not_45_out, Received_6_Bits_Message[2]);
  not not_46 (not_46_out, Received_6_Bits_Message[5]);
  not not_47 (not_47_out, Received_6_Bits_Message[0]);
  not not_48 (not_48_out, Received_6_Bits_Message[3]);
  not not_49 (not_49_out, Received_6_Bits_Message[4]);
  not not_50 (not_50_out, Received_6_Bits_Message[0]);
  not not_51 (not_51_out, Received_6_Bits_Message[3]);
  not not_52 (not_52_out, Received_6_Bits_Message[5]);
  not not_53 (not_53_out, Received_6_Bits_Message[0]);
  not not_54 (not_54_out, Received_6_Bits_Message[4]);
  not not_55 (not_55_out, Received_6_Bits_Message[5]);
  not not_56 (not_56_out, Received_6_Bits_Message[0]);
  not not_57 (not_57_out, Received_6_Bits_Message[1]);
  not not_58 (not_58_out, Received_6_Bits_Message[2]);
  not not_59 (not_59_out, Received_6_Bits_Message[3]);
  not not_60 (not_60_out, Received_6_Bits_Message[4]);
  not not_61 (not_61_out, Received_6_Bits_Message[5]);
  not not_62 (not_62_out, Received_6_Bits_Message[1]);
  not not_63 (not_63_out, Received_6_Bits_Message[2]);
  not not_64 (not_64_out, Received_6_Bits_Message[3]);
  not not_65 (not_65_out, Received_6_Bits_Message[1]);
  not not_66 (not_66_out, Received_6_Bits_Message[2]);
  not not_67 (not_67_out, Received_6_Bits_Message[4]);
  not not_68 (not_68_out, Received_6_Bits_Message[1]);
  not not_69 (not_69_out, Received_6_Bits_Message[2]);
  not not_70 (not_70_out, Received_6_Bits_Message[5]);
  not not_71 (not_71_out, Received_6_Bits_Message[1]);
  not not_72 (not_72_out, Received_6_Bits_Message[3]);
  not not_73 (not_73_out, Received_6_Bits_Message[4]);
  not not_74 (not_74_out, Received_6_Bits_Message[1]);
  not not_75 (not_75_out, Received_6_Bits_Message[3]);
  not not_76 (not_76_out, Received_6_Bits_Message[5]);
  not not_77 (not_77_out, Received_6_Bits_Message[1]);
  not not_78 (not_78_out, Received_6_Bits_Message[4]);
  not not_79 (not_79_out, Received_6_Bits_Message[5]);
  not not_80 (not_80_out, Received_6_Bits_Message[1]);
  not not_81 (not_81_out, Received_6_Bits_Message[2]);
  not not_82 (not_82_out, Received_6_Bits_Message[3]);
  not not_83 (not_83_out, Received_6_Bits_Message[4]);
  not not_84 (not_84_out, Received_6_Bits_Message[2]);
  not not_85 (not_85_out, Received_6_Bits_Message[3]);
  not not_86 (not_86_out, Received_6_Bits_Message[5]);
  not not_87 (not_87_out, Received_6_Bits_Message[2]);
  not not_88 (not_88_out, Received_6_Bits_Message[4]);
  not not_89 (not_89_out, Received_6_Bits_Message[5]);
  not not_90 (not_90_out, Received_6_Bits_Message[2]);
  not not_91 (not_91_out, Received_6_Bits_Message[3]);
  not not_92 (not_92_out, Received_6_Bits_Message[4]);
  not not_93 (not_93_out, Received_6_Bits_Message[5]);
  not not_94 (not_94_out, Received_6_Bits_Message[3]);
  not not_95 (not_95_out, Received_6_Bits_Message[4]);
  not not_96 (not_96_out, Received_6_Bits_Message[5]);
  and and_1 (and_1_out, not_1_out, not_2_out, not_3_out, not_4_out, not_5_out, Received_6_Bits_Message[5]);
  and and_2 (and_2_out, not_6_out, not_7_out, not_8_out, not_9_out, Received_6_Bits_Message[4], not_10_out);
  and and_3 (and_3_out, not_11_out, not_12_out, not_13_out, Received_6_Bits_Message[3], not_14_out, not_15_out);
  and and_4 (and_4_out, not_16_out, not_17_out, not_18_out, Received_6_Bits_Message[3], Received_6_Bits_Message[4], Received_6_Bits_Message[5]);
  and and_5 (and_5_out, not_19_out, not_20_out, Received_6_Bits_Message[2], not_21_out, not_22_out, not_23_out);
  and and_6 (and_6_out, not_24_out, not_25_out, Received_6_Bits_Message[2], not_26_out, Received_6_Bits_Message[4], Received_6_Bits_Message[5]);
  and and_7 (and_7_out, not_27_out, not_28_out, Received_6_Bits_Message[2], Received_6_Bits_Message[3], not_29_out, Received_6_Bits_Message[5]);
  and and_8 (and_8_out, not_30_out, not_31_out, Received_6_Bits_Message[2], Received_6_Bits_Message[3], Received_6_Bits_Message[4], not_32_out);
  and and_9 (and_9_out, not_33_out, Received_6_Bits_Message[1], not_34_out, not_35_out, not_36_out, not_37_out);
  and and_10 (and_10_out, not_38_out, Received_6_Bits_Message[1], not_39_out, not_40_out, Received_6_Bits_Message[4], Received_6_Bits_Message[5]);
  and and_11 (and_11_out, not_41_out, Received_6_Bits_Message[1], not_42_out, Received_6_Bits_Message[3], not_43_out, Received_6_Bits_Message[5]);
  and and_12 (and_12_out, not_44_out, Received_6_Bits_Message[1], not_45_out, Received_6_Bits_Message[3], Received_6_Bits_Message[4], not_46_out);
  and and_13 (and_13_out, not_47_out, Received_6_Bits_Message[1], Received_6_Bits_Message[2], not_48_out, not_49_out, Received_6_Bits_Message[5]);
  and and_14 (and_14_out, not_50_out, Received_6_Bits_Message[1], Received_6_Bits_Message[2], not_51_out, Received_6_Bits_Message[4], not_52_out);
  and and_15 (and_15_out, not_53_out, Received_6_Bits_Message[1], Received_6_Bits_Message[2], Received_6_Bits_Message[3], not_54_out, not_55_out);
  and and_16 (and_16_out, not_56_out, Received_6_Bits_Message[1], Received_6_Bits_Message[2], Received_6_Bits_Message[3], Received_6_Bits_Message[4], Received_6_Bits_Message[5]);
  and and_17 (and_17_out, Received_6_Bits_Message[0], not_57_out, not_58_out, not_59_out, not_60_out, not_61_out);
  and and_18 (and_18_out, Received_6_Bits_Message[0], not_62_out, not_63_out, not_64_out, Received_6_Bits_Message[4], Received_6_Bits_Message[5]);
  and and_19 (and_19_out, Received_6_Bits_Message[0], not_65_out, not_66_out, Received_6_Bits_Message[3], not_67_out, Received_6_Bits_Message[5]);
  and and_20 (and_20_out, Received_6_Bits_Message[0], not_68_out, not_69_out, Received_6_Bits_Message[3], Received_6_Bits_Message[4], not_70_out);
  and and_21 (and_21_out, Received_6_Bits_Message[0], not_71_out, Received_6_Bits_Message[2], not_72_out, not_73_out, Received_6_Bits_Message[5]);
  and and_22 (and_22_out, Received_6_Bits_Message[0], not_74_out, Received_6_Bits_Message[2], not_75_out, Received_6_Bits_Message[4], not_76_out);
  and and_23 (and_23_out, Received_6_Bits_Message[0], not_77_out, Received_6_Bits_Message[2], Received_6_Bits_Message[3], not_78_out, not_79_out);
  and and_24 (and_24_out, Received_6_Bits_Message[0], not_80_out, Received_6_Bits_Message[2], Received_6_Bits_Message[3], Received_6_Bits_Message[4], Received_6_Bits_Message[5]);
  and and_25 (and_25_out, Received_6_Bits_Message[0], Received_6_Bits_Message[1], not_81_out, not_82_out, not_83_out, Received_6_Bits_Message[5]);
  and and_26 (and_26_out, Received_6_Bits_Message[0], Received_6_Bits_Message[1], not_84_out, not_85_out, Received_6_Bits_Message[4], not_86_out);
  and and_27 (and_27_out, Received_6_Bits_Message[0], Received_6_Bits_Message[1], not_87_out, Received_6_Bits_Message[3], not_88_out, not_89_out);
  and and_28 (and_28_out, Received_6_Bits_Message[0], Received_6_Bits_Message[1], not_90_out, Received_6_Bits_Message[3], Received_6_Bits_Message[4], Received_6_Bits_Message[5]);
  and and_29 (and_29_out, Received_6_Bits_Message[0], Received_6_Bits_Message[1], Received_6_Bits_Message[2], not_91_out, not_92_out, not_93_out);
  and and_30 (and_30_out, Received_6_Bits_Message[0], Received_6_Bits_Message[1], Received_6_Bits_Message[2], not_94_out, Received_6_Bits_Message[4], Received_6_Bits_Message[5]);
  and and_31 (and_31_out, Received_6_Bits_Message[0], Received_6_Bits_Message[1], Received_6_Bits_Message[2], Received_6_Bits_Message[3], not_95_out, Received_6_Bits_Message[5]);
  and and_32 (and_32_out, Received_6_Bits_Message[0], Received_6_Bits_Message[1], Received_6_Bits_Message[2], Received_6_Bits_Message[3], Received_6_Bits_Message[4], not_96_out);
  or or_1 (Is_Data_Changed, and_1_out, and_2_out, and_3_out, and_4_out, and_5_out, and_6_out, and_7_out, and_8_out, and_9_out, and_10_out, and_11_out, and_12_out, and_13_out, and_14_out, and_15_out, and_16_out, and_17_out, and_18_out, and_19_out, and_20_out, and_21_out, and_22_out, and_23_out, and_24_out, and_25_out, and_26_out, and_27_out, and_28_out, and_29_out, and_30_out, and_31_out, and_32_out);
endmodule
