// Logisim project circuit.circ as structural Verilog: 3 circuits, main circuit main
module main (
  input  [4:0] Input,
  input  [4:0] Input_2,
  output Is_Data_Changed,
  output Is_Data_Changed_2
);

  wire [5:0] not_1_out, Sender_2_msb_is_parity_bit, Sender_msb_is_parity_bit;

  Generator_Or_Sender Sender (._5_Bits_Input(Input), .MSB_is_Parity_bit(Sender_msb_is_parity_bit));
  Generator_Or_Sender Sender_2 (._5_Bits_Input(Input_2), .MSB_is_Parity_bit(Sender_2_msb_is_parity_bit));
  assign not_1_out = ~Sender_2_msb_is_parity_bit;  // NOT_Gate not_1, 6 bits wide
  Checker_Or_Receiver Receiver (.Input(Sender_msb_is_parity_bit), .Is_data_changed(Is_Data_Changed));
  Checker_Or_Receiver Receiver_2 (.Input(not_1_out), .Is_data_changed(Is_Data_Changed_2));

  // Notes on the sheet:
  //   Case 1: If we don't manipulate data
  //   Case 2: If we manipulate data
endmodule

module Generator_Or_Sender (
  input  [4:0] _5_Bits_Input,
  output [5:0] MSB_is_Parity_bit
);

  wire xor_1_out, xor_2_out, xor_3_out;

  xor xor_1 (xor_1_out, _5_Bits_Input[0], _5_Bits_Input[1]);
  xor xor_2 (xor_2_out, _5_Bits_Input[2], _5_Bits_Input[3]);
  xor xor_3 (xor_3_out, xor_2_out, _5_Bits_Input[4]);
  xor xor_4 (MSB_is_Parity_bit[5], xor_1_out, xor_3_out);

  assign MSB_is_Parity_bit[4:0] = _5_Bits_Input;

  // Notes on the sheet:
  //   5 Bits Even Parity Generator
endmodule

module Checker_Or_Receiver (
  input  [5:0] Input,
  output Is_data_changed
);

  wire xor_1_out, xor_2_out, xor_3_out, xor_4_out;

  xor xor_1 (xor_1_out, Input[0], Input[1]);
  xor xor_2 (xor_2_out, Input[2], Input[3]);
  xor xor_3 (xor_3_out, Input[4], Input[5]);
  xor xor_4 (xor_4_out, xor_1_out, xor_2_out);
  xor xor_5 (Is_data_changed, xor_4_out, xor_3_out);

  // Notes on the sheet:
  //   5 Bits Even Parity Checker
endmodule
